// Logisim project Logique.circ as structural Verilog: 1 circuit, main circuit ACAR
module ACAR (
  input  A,
  input  D,
  input  B,
  input  C
);

  wire not_1_out, not_2_out, or_1_out, or_2_out;

  LED Right_Motor (.in(not_1_out));
  not not_1 (not_1_out, or_1_out);
  or or_1 (or_1_out, A, B);
  LED Left_Motor (.in(not_2_out));
  not not_2 (not_2_out, or_2_out);
  or or_2 (or_2_out, C, D);
endmodule
